// Logisim project clocked-counter.circ as structural Verilog: 1 circuit, main circuit main
module main (
  output [3:0] q,
  output halt
);

  wire clock_1_out;

  Clock clock_1 (.out(clock_1_out));
  Counter #(.width(4), .max('hf)) counter_1 (.Q(q), .carry(halt), .clk(clock_1_out));  // open: load, D, count, up, clr
endmodule
