// Logisim project combinational.circ as structural Verilog: 1 circuit, main circuit main
module main (
  input  A,
  input  B,
  input  C,
  output Y,
  output Z
);

  wire and_1_out;

  and and_1 (and_1_out, A, B);
  or or_1 (Y, and_1_out, C);
  xor xor_1 (Z, A, C);
endmodule
