// Logisim project legacy-2.7-format.circ as structural Verilog: 1 circuit, main circuit main
module main (
  input  A,
  input  B,
  input  C,
  output Y,
  output Cbuf
);

  nand nand_1 (Y, A, B);

  assign Cbuf = C;
endmodule
