// Logisim project multibit-adder.circ as structural Verilog: 1 circuit, main circuit main
module main (
  input  [3:0] A,
  input  [3:0] B,
  output [3:0] S,
  output Cout
);

  Adder #(.width(4)) adder_1 (.a(A), .b(B), .out(S), .cout(Cout));  // open: cin
endmodule
