// Logisim project subcircuit-custom-appearance.circ as structural Verilog: 2 circuits, main circuit main
module main (
  input  A,
  input  B,
  input  Cin,
  output S,
  output Cout
);

  wire half_adder_1_c, half_adder_1_s, half_adder_2_c;

  half_adder half_adder_1 (.a(A), .b(B), .s(half_adder_1_s), .c(half_adder_1_c));
  half_adder half_adder_2 (.a(half_adder_1_s), .b(Cin), .s(S), .c(half_adder_2_c));
  or or_1 (Cout, half_adder_2_c, half_adder_1_c);
endmodule

module half_adder (
  input  a,
  input  b,
  output s,
  output c
);

  xor xor_1 (s, a, b);
  and and_1 (c, a, b);
endmodule
